# Fritzing sketch cat_robot_distance_remote (saved by Fritzing 0.9.3b)
breadboards: 1

parts:
  IR1 = TSOP312.., 314.. [package=THT]
  hc-sr1 = hc-sr04
  Part2 = Arduino Uno (Rev3)
  J1 = Basic Servo
  J2 = Basic Servo
  BAT1 = BC9VPC [package=bc9vpc]  # not connected

nets:
  GND: IR1.GND, hc-sr1.GND, Part2.GND, J1.gnd, J2.gnd
  VCC: IR1.Vs, hc-sr1.VCC, Part2.5V, J1.vcc, J2.vcc
  N1: IR1.Data, Part2.D12/MISO
  N2: hc-sr1.Trig, Part2.D2
  N3: hc-sr1.Echo, Part2.D4
  N4: Part2.D8, J1.pulse
  N5: Part2.D9_PWM, J2.pulse
